# Fritzing sketch magiclockbox (saved by Fritzing 0.9.3b)
breadboards: 1

parts:
  Mod1 = azure-sphere_1 [part_number=azsphere]
  J1 = Basic Servo [part_number=sg90]
  Q1 = NPN-Transistor [part_number=2N3904 package="TO92 [THT]"]
  Q2 = PNP-Transistor [part_number=2N5401 package="TO92 [THT]"]
  R2 = Resistor [tolerance=±5% resistance=33 package=THT]
  R3 = Resistor [tolerance=±5% resistance=1k package=THT]
  J3 = shrouded pin header, 40 pins [form="♂ (shrouded male)" part_number="MGC3130 SHIELD"]
  J2 = shrouded pin header, 6 pins [form="♂ (shrouded male)" part_number="GROVE I2C"]

nets (from the schematic view):
  N1: Mod1.connector6, J3.pin17
  GND: Mod1.connector7, J1.gnd, Q1.E
  N2: Mod1.connector8, J1.pulse
  N3: Mod1.connector9, R3.Pin_1
  ts: Mod1.connector10, J3.pin7
  rst: Mod1.connector11, J3.pin11
  N4: Mod1.connector14, Q2.E
  N5: Mod1.connector48, J2.pin4
  N6: Mod1.connector49, J2.pin3
  N7: Mod1.connector50, J2.pin2
  N8: Mod1.connector51, J2.pin1
  N9: J1.vcc, Q2.C
  N10: Q1.B, R3.Pin_0
  N11: Q1.C, R2.Pin_0
  N12: Q2.B, R2.Pin_1
